// Logisim project sapcpu1.circ as structural Verilog: 2 circuits, main circuit main
// Reg
module main (
  input  [7:0] I__Input,
  input  AI,
  input  AU,
  input  BI,
  input  BU,
  input  EU,
  input  IU,
  input  OI,
  output [7:0] out_9,
  output [7:0] E__ALU,
  output [7:0] O__Output,
  output [7:0] out_12,
  output [7:0] out_13
);

  wire Klokke__K_out;

  Clock Klokke__K (.out(Klokke__K_out));
  Register A (.D(out_13), .CLK(Klokke__K_out), .RI(AI), .RO(AU), .Q(out_13), .V(out_9));
  Register B (.D(out_13), .CLK(Klokke__K_out), .RI(BI), .RO(BU), .Q(out_13), .V(out_12));
  assign out_13 = EU ? E__ALU : 8'bz;  // Controlled_Buffer controlled_buffer_1
  Adder adder_1 (.a(out_9), .b(out_12), .out(E__ALU));  // open: cin, cout
  assign out_13 = IU ? I__Input : 8'bz;  // Controlled_Buffer controlled_buffer_2
  Register register_1 (.D(out_13), .CLK(Klokke__K_out), .RI(OI), .V(O__Output));  // open: RO, Q

  // Notes on the sheet:
  //   SAP-1 inspireret 8 bit computer - version 1
  //   Michell Cronberg
  //   8 bit databus
endmodule

module Register (
  input  RO,
  input  [7:0] D,
  input  CLK,
  input  RI,
  output [7:0] Q,
  output [7:0] V
);

  wire [7:0] controlled_buffer_1_out;

  assign controlled_buffer_1_out = RI ? D : 8'bz;  // Controlled_Buffer controlled_buffer_1
  Register_part register_1 (.D(controlled_buffer_1_out), .en(1'b1), .Q(V), .clk(CLK), .clr(1'b0));
  assign Q = RO ? V : 8'bz;  // Controlled_Buffer controlled_buffer_2
endmodule
