// Logisim project sapcpu2.circ as structural Verilog: 2 circuits, main circuit main
// Reg
module main (
  input  [7:0] I__Input,
  input  AI,
  input  AU,
  input  BI,
  input  BU,
  input  EU,
  input  IU,
  input  OI,
  input  MI,
  input  RU,
  output [7:0] out_11,
  output [7:0] E__ALU,
  output [7:0] O__Output,
  output [7:0] MAR,
  output [7:0] out_15,
  output [7:0] out_16
);

  wire Klokke__K_out;
  wire [7:0] ram_1_data;

  Clock Klokke__K (.out(Klokke__K_out));
  Register A (.D(out_16), .CLK(Klokke__K_out), .RI(AI), .RO(AU), .Q(out_16), .V(out_11));
  Register B (.D(out_16), .CLK(Klokke__K_out), .RI(BI), .RO(BU), .Q(out_16), .V(out_15));
  assign out_16 = EU ? E__ALU : 8'bz;  // Controlled_Buffer controlled_buffer_1
  Adder adder_1 (.a(out_11), .b(out_15), .out(E__ALU));  // open: cin, cout
  assign out_16 = IU ? I__Input : 8'bz;  // Controlled_Buffer controlled_buffer_2
  Register register_1 (.D(out_16), .CLK(Klokke__K_out), .RI(OI), .V(O__Output));  // open: RO, Q
  Register M_AR (.D(out_16), .CLK(Klokke__K_out), .RI(MI), .V(MAR));  // open: RO, Q
  assign out_16 = RU ? ram_1_data : 8'bz;  // Controlled_Buffer controlled_buffer_3
  RAM ram_1 (.addr(MAR), .data(ram_1_data), .clk(Klokke__K_out));  // open: sel, ld, clr

  // Notes on the sheet:
  //   SAP-1 inspireret 8 bit computer - version 2
  //   Michell Cronberg
  //   8 bit databus
  //   (R)AM
endmodule

module Register (
  input  RO,
  input  [7:0] D,
  input  CLK,
  input  RI,
  output [7:0] Q,
  output [7:0] V
);

  wire [7:0] controlled_buffer_1_out;

  assign controlled_buffer_1_out = RI ? D : 8'bz;  // Controlled_Buffer controlled_buffer_1
  Register_part register_1 (.D(controlled_buffer_1_out), .en(1'b1), .Q(V), .clk(CLK), .clr(1'b0));
  assign Q = RO ? V : 8'bz;  // Controlled_Buffer controlled_buffer_2
endmodule
