// Logisim project sapcpu4.circ as structural Verilog: 7 circuits, main circuit Main
// Reg
module Main (
  input  [7:0] I__Input,
  output [7:0] out_2,
  output [7:0] out_3,
  output [7:0] out_4,
  output [7:0] E__ALU,
  output [7:0] O__Output,
  output [7:0] MAR,
  output [7:0] out_8,
  output [7:0] out_9,
  output [7:0] out_10
);

  wire comparator_1_lt, controlled_buffer_1_out, Klokke__K_out, not_1_out, not_2_out, not_3_out, RESET_out;
  wire [7:0] IR_l, ram_1_data;
  wire [15:0] adder_1_out, controlled_buffer_3_out, counter_1_q, IR_h, rom_1_data;

  Clock Klokke__K (.out(Klokke__K_out));
  assign controlled_buffer_1_out = not_2_out ? Klokke__K_out : 1'bz;  // Controlled_Buffer controlled_buffer_1
  InstruktionRegister IR (
    .A(out_9), .CLK(controlled_buffer_1_out), .RI(rom_1_data[3]), .RO(rom_1_data[2]), .L(IR_l), .V(out_10),
    .H(IR_h));  // open: Q
  Counter #(.width(16), .max('h5)) counter_1 (
    .Q(counter_1_q), .clk(controlled_buffer_1_out), .clr(RESET_out));  // open: load, D, count, carry
  Register A (.D(out_9), .CLK(controlled_buffer_1_out), .RI(rom_1_data[15]), .RO(rom_1_data[14]), .Q(out_9), .V(out_4));
  Register B (.D(out_9), .CLK(controlled_buffer_1_out), .RI(rom_1_data[13]), .RO(rom_1_data[12]), .Q(out_9), .V(out_8));
  assign out_9 = rom_1_data[2] ? IR_l : 8'bz;  // Controlled_Buffer controlled_buffer_2
  Adder #(.width(16)) adder_1 (.a(IR_h), .b(counter_1_q), .out(adder_1_out));  // open: cin, cout
  Comparator #(.width(16)) comparator_1 (.a(counter_1_q), .b(16'h3), .lt(comparator_1_lt));  // open: gt, eq
  assign controlled_buffer_3_out = comparator_1_lt ? counter_1_q : 16'bz;  // Controlled_Buffer controlled_buffer_3
  Adder adder_2 (.a(out_4), .b(out_8), .out(E__ALU));  // open: cin, cout
  assign out_9 = rom_1_data[11] ? E__ALU : 8'bz;  // Controlled_Buffer controlled_buffer_4
  assign controlled_buffer_3_out = not_1_out ? adder_1_out : 16'bz;  // Controlled_Buffer controlled_buffer_5
  not not_1 (not_1_out, comparator_1_lt);
  assign out_9 = rom_1_data[10] ? I__Input : 8'bz;  // Controlled_Buffer controlled_buffer_6
  Register register_1 (.D(out_9), .CLK(controlled_buffer_1_out), .RI(rom_1_data[9]), .V(O__Output));  // open: RO, Q
  ROM #(.addrWidth(16), .dataWidth(16)) rom_1 (.addr(controlled_buffer_3_out), .data(rom_1_data));  // open: sel
  Register M_AR (.D(out_9), .CLK(controlled_buffer_1_out), .RI(rom_1_data[8]), .V(MAR));  // open: RO, Q
  not not_2 (not_2_out, rom_1_data[1]);
  not not_3 (not_3_out, rom_1_data[0]);
  assign out_3 = rom_1_data[5] ? out_9 : 8'bz;  // Controlled_Buffer controlled_buffer_7
  assign out_9 = rom_1_data[7] ? ram_1_data : 8'bz;  // Controlled_Buffer controlled_buffer_8
  RAM #(.bus("separate")) ram_1 (
    .addr(MAR), .din(out_9), .data(ram_1_data), .str(rom_1_data[0]), .sel(1'b1),
    .clk(controlled_buffer_1_out), .ld(not_3_out));  // open: clr
  ProgramCounter PC (.S(rom_1_data[5]), .A(out_3), .Count(rom_1_data[6]), .Q(out_2), .Reset(RESET_out));
  assign out_9 = rom_1_data[4] ? out_2 : 8'bz;  // Controlled_Buffer controlled_buffer_9
  Button RESET (.out(RESET_out));

  // Notes on the sheet:
  //   SAP-1 inspireret 8 bit computer - version 4
  //   Michell Cronberg
  //   Mikro tæller
  //   BI
  //   AU
  //   AI
  //   EU
  //   IU
  //   BU
  //   8 bit databus
  //   OI
  //   MI
  //   RI
  //   II
  //   IU
  //   RU
  //   PI
  //   KS (Klokke stop)
  //   contents of rom_1 (hex, n*v repeats v):
  //   110 88 40 16*0 104 8080 14*0 104 2080 8800 13*0 4200 15*0 2 15*0 104 4001 14*0 8004 15*0 24 64 14*0
  //   6000
  //   PT (tæl program)
  //   PU
  //   (R)AM
endmodule

module Register (
  input  RO,
  input  [7:0] D,
  input  CLK,
  input  RI,
  output [7:0] Q,
  output [7:0] V
);

  wire [7:0] controlled_buffer_1_out;

  assign controlled_buffer_1_out = RI ? D : 8'bz;  // Controlled_Buffer controlled_buffer_1
  Register_part register_1 (.D(controlled_buffer_1_out), .en(1'b1), .Q(V), .clk(CLK), .clr(1'b0));
  assign Q = RO ? V : 8'bz;  // Controlled_Buffer controlled_buffer_2
endmodule

module ProgramCounter (
  input  S,
  input  [7:0] A,
  input  Count,
  input  Reset,
  output [7:0] Q
);

  wire not_1_out;

  not not_1 (not_1_out, S);
  Counter counter_1 (.load(S), .D(A), .count(not_1_out), .Q(Q), .clk(Count), .clr(Reset));  // open: carry
endmodule

module SplitByteLower4 (
  input  [7:0] A,
  output [7:0] Q
);


  assign Q = {4'b0000, A[3:0]};
endmodule

module MircoInstructionAddress (
  input  [3:0] in_1,
  output [15:0] out_2
);


  assign out_2 = {{8{1'b0}}, in_1, 4'b0000};
endmodule

module SplitByteHigh16 (
  input  [7:0] A,
  output [15:0] Q
);


  assign Q = {{8{1'b0}}, A[7:4], 4'b0000};
endmodule

module InstruktionRegister (
  input  [7:0] A,
  input  CLK,
  input  RI,
  input  RO,
  output [7:0] L,
  output [7:0] Q,
  output [7:0] V,
  output [15:0] H
);

  Register register_1 (.D(A), .CLK(CLK), .RI(RI), .RO(RO), .Q(Q), .V(V));
  SplitByteLower4 splitbytelower4_1 (.A(V), .Q(L));
  SplitByteHigh16 splitbytehigh16_1 (.A(V), .Q(H));
endmodule
