// Logisim project sapcpu2.circ as structural Verilog: 2 circuits, main circuit main
// Reg
module main (
  input  [7:0] I__Input,
  input  AI,
  input  AO,
  input  BI,
  input  BO,
  input  EO,
  input  IO,
  input  OI,
  input  MI,
  input  RO,
  output [7:0] out_11,
  output [7:0] E__ALU,
  output [7:0] O__Output,
  output [7:0] MAR,
  output [7:0] out_15,
  output [7:0] out_16
);

  wire CLK_out;
  wire [7:0] ram_1_data;

  Clock CLK (.out(CLK_out));
  Register A (.D(out_16), .CLK(CLK_out), .RI(AI), .RO(AO), .Q(out_16), .V(out_11));
  Register B (.D(out_16), .CLK(CLK_out), .RI(BI), .RO(BO), .Q(out_16), .V(out_15));
  Adder adder_1 (.a(out_11), .b(out_15), .out(E__ALU));  // open: cin, cout
  assign out_16 = EO ? E__ALU : 8'bz;  // Controlled_Buffer controlled_buffer_1
  assign out_16 = IO ? I__Input : 8'bz;  // Controlled_Buffer controlled_buffer_2
  Register register_1 (.D(out_16), .CLK(CLK_out), .RI(OI), .V(O__Output));  // open: RO, Q
  Register M_AR (.D(out_16), .CLK(CLK_out), .RI(MI), .V(MAR));  // open: RO, Q
  RAM ram_1 (.addr(MAR), .data(ram_1_data), .clk(CLK_out));  // open: sel, ld, clr
  assign out_16 = RO ? ram_1_data : 8'bz;  // Controlled_Buffer controlled_buffer_3

  // Notes on the sheet:
  //   SAP-1 inspireret 8 bit computer - version 2
  //   Michell Cronberg
  //   8 bit databus
  //   (R)AM
endmodule

module Register (
  input  RO,
  input  [7:0] D,
  input  CLK,
  input  RI,
  output [7:0] Q,
  output [7:0] V
);

  wire [7:0] controlled_buffer_1_out;

  assign controlled_buffer_1_out = RI ? D : 8'bz;  // Controlled_Buffer controlled_buffer_1
  Register_part register_1 (.D(controlled_buffer_1_out), .en(1'b1), .Q(V), .clk(CLK), .clr(1'b0));
  assign Q = RO ? V : 8'bz;  // Controlled_Buffer controlled_buffer_2
endmodule
