// Logisim project sapcpu4a.circ as structural Verilog: 11 circuits, main circuit main
// Reg
module main (
  input  [7:0] K__Input,
  output [7:0] out_2,
  output [7:0] out_3,
  output [7:0] out_4,
  output [7:0] E__ALU,
  output [7:0] MAR,
  output [7:0] out_7,
  output [7:0] out_8,
  output [7:0] out_9
);

  wire CLK_out, comparator_1_lt, controlled_buffer_1_out, not_1_out, not_2_out, not_3_out, RESET_out;
  wire [3:0] highbites_1_q, lowbites_1_q;
  wire [7:0] instruktionregister_1_l, ram_1_data, register_1_v;
  wire [15:0] adder_1_out, controlled_buffer_3_out, counter_1_q, instruktionregister_1_h, rom_1_data;

  Clock CLK (.out(CLK_out));
  assign controlled_buffer_1_out = not_2_out ? CLK_out : 1'bz;  // Controlled_Buffer controlled_buffer_1
  InstruktionRegister instruktionregister_1 (
    .A(out_8), .CLK(controlled_buffer_1_out), .RI(rom_1_data[3]), .RO(rom_1_data[2]),
    .L(instruktionregister_1_l), .V(out_9), .H(instruktionregister_1_h));  // open: Q
  Counter #(.width(16), .max('h5)) counter_1 (
    .Q(counter_1_q), .clk(controlled_buffer_1_out), .clr(RESET_out));  // open: load, D, count, carry
  Register A (.D(out_8), .CLK(controlled_buffer_1_out), .RI(rom_1_data[15]), .RO(rom_1_data[14]), .Q(out_8), .V(out_4));
  Register B (.D(out_8), .CLK(controlled_buffer_1_out), .RI(rom_1_data[13]), .RO(rom_1_data[12]), .Q(out_8), .V(out_7));
  assign out_8 = rom_1_data[2] ? instruktionregister_1_l : 8'bz;  // Controlled_Buffer controlled_buffer_2
  Adder #(.width(16)) adder_1 (.a(instruktionregister_1_h), .b(counter_1_q), .out(adder_1_out));  // open: cin, cout
  Comparator #(.width(16)) comparator_1 (.a(counter_1_q), .b(16'h3), .lt(comparator_1_lt));  // open: gt, eq
  assign controlled_buffer_3_out = comparator_1_lt ? counter_1_q : 16'bz;  // Controlled_Buffer controlled_buffer_3
  Adder adder_2 (.a(out_4), .b(out_7), .out(E__ALU));  // open: cin, cout
  assign out_8 = rom_1_data[11] ? E__ALU : 8'bz;  // Controlled_Buffer controlled_buffer_4
  assign controlled_buffer_3_out = not_1_out ? adder_1_out : 16'bz;  // Controlled_Buffer controlled_buffer_5
  not not_1 (not_1_out, comparator_1_lt);
  assign out_8 = rom_1_data[10] ? K__Input : 8'bz;  // Controlled_Buffer controlled_buffer_6
  Register register_1 (.D(out_8), .CLK(controlled_buffer_1_out), .RI(rom_1_data[9]), .V(register_1_v));  // open: RO, Q
  ROM #(.addrWidth(16), .dataWidth(16)) rom_1 (.addr(controlled_buffer_3_out), .data(rom_1_data));  // open: sel
  DotMatrix #(.matrixcols(8), .matrixrows(1)) dotmatrix_1 (
    .col0(register_1_v[7]), .col1(register_1_v[6]), .col2(register_1_v[5]), .col3(register_1_v[4]),
    .col4(register_1_v[3]), .col5(register_1_v[2]), .col6(register_1_v[1]), .col7(register_1_v[0]));
  Register M_AR (.D(out_8), .CLK(controlled_buffer_1_out), .RI(rom_1_data[8]), .V(MAR));  // open: RO, Q
  not not_2 (not_2_out, rom_1_data[1]);
  not not_3 (not_3_out, rom_1_data[0]);
  assign out_3 = rom_1_data[5] ? out_8 : 8'bz;  // Controlled_Buffer controlled_buffer_7
  RAM #(.bus("separate")) ram_1 (
    .addr(MAR), .din(out_8), .data(ram_1_data), .str(rom_1_data[0]), .sel(1'b1),
    .clk(controlled_buffer_1_out), .ld(not_3_out));  // open: clr
  assign out_8 = rom_1_data[7] ? ram_1_data : 8'bz;  // Controlled_Buffer controlled_buffer_8
  ProgramCounter PC (.S(rom_1_data[5]), .A(out_3), .Count(rom_1_data[6]), .Q(out_2), .Reset(RESET_out));
  assign out_8 = rom_1_data[4] ? out_2 : 8'bz;  // Controlled_Buffer controlled_buffer_9
  Button RESET (.out(RESET_out));
  Hex_Digit_Display hex_digit_display_1 (.value(highbites_1_q));  // open: dp
  HighBites highbites_1 (.A(register_1_v), .Q(highbites_1_q));
  LowBites lowbites_1 (.A(register_1_v), .Q(lowbites_1_q));
  Hex_Digit_Display hex_digit_display_2 (.value(lowbites_1_q));  // open: dp

  // Notes on the sheet:
  //   SAP-1 inspireret 8 bit computer - version 4
  //   Michell Cronberg
  //   BI
  //   AO
  //   AI
  //   BO
  //   EO
  //   KO
  //   8 bit databus
  //   MI
  //   OI
  //   II
  //   IO
  //   RO
  //   PE
  //   PI
  //   contents of rom_1 (hex, n*v repeats v):
  //   110 88 40 16*0 104 8080 14*0 104 2080 8800 13*0 4200 15*0 2 15*0 104 4001 14*0 8004 15*0 24 64 14*0
  //   6000
  //   (O)utput
  //   PO
  //   (R)AM
endmodule

module Register (
  input  RO,
  input  [7:0] D,
  input  CLK,
  input  RI,
  output [7:0] Q,
  output [7:0] V
);

  wire [7:0] controlled_buffer_1_out;

  assign controlled_buffer_1_out = RI ? D : 8'bz;  // Controlled_Buffer controlled_buffer_1
  Register_part register_1 (.D(controlled_buffer_1_out), .en(1'b1), .Q(V), .clk(CLK), .clr(1'b0));
  assign Q = RO ? V : 8'bz;  // Controlled_Buffer controlled_buffer_2
endmodule

module ProgramCounter (
  input  S,
  input  [7:0] A,
  input  Count,
  input  Reset,
  output [7:0] Q
);

  wire not_1_out;

  not not_1 (not_1_out, S);
  Counter counter_1 (.load(S), .D(A), .count(not_1_out), .Q(Q), .clk(Count), .clr(Reset));  // open: carry
endmodule

module SplitByteLower4 (
  input  [7:0] A,
  output [7:0] Q
);


  assign Q = {4'b0000, A[3:0]};
endmodule

module MircoInstructionAddress (
  input  [3:0] in_1,
  output [15:0] out_2
);


  assign out_2 = {{8{1'b0}}, in_1, 4'b0000};
endmodule

module Temp (
  output [7:0] out_1
);

  wire button_1_out;

  Button button_1 (.out(button_1_out));
  Counter #(.max('h5)) counter_1 (.Q(out_1), .clk(button_1_out));  // open: load, D, count, carry, clr
endmodule

module SplitByteHigh16 (
  input  [7:0] A,
  output [15:0] Q
);


  assign Q = {{8{1'b0}}, A[7:4], 4'b0000};
endmodule

module InstruktionRegister (
  input  [7:0] A,
  input  CLK,
  input  RI,
  input  RO,
  output [7:0] L,
  output [7:0] Q,
  output [7:0] V,
  output [15:0] H
);

  Register register_1 (.D(A), .CLK(CLK), .RI(RI), .RO(RO), .Q(Q), .V(V));
  SplitByteLower4 splitbytelower4_1 (.A(V), .Q(L));
  SplitByteHigh16 splitbytehigh16_1 (.A(V), .Q(H));
endmodule

module SplitByteHigh4 (
  input  [7:0] A,
  output [7:0] Q
);


  assign Q = {A[7:4], 4'b0000};
endmodule

module HighBites (
  input  [7:0] A,
  output [3:0] Q
);


  assign Q = A[7:4];
endmodule

module LowBites (
  input  [7:0] A,
  output [3:0] Q
);


  assign Q = A[3:0];
endmodule
