// Logisim project temp.circ as structural Verilog: 3 circuits, main circuit main
// Reg
module main (
  input  [7:0] I__Input,
  output [7:0] out_2,
  output [7:0] E__ALU,
  output [7:0] O__Output,
  output [7:0] MAR,
  output [7:0] out_6,
  output [7:0] out_7
);

  wire CLK_out;
  wire [7:0] ram_1_data;
  wire [15:0] rom_1_data;

  Clock CLK (.out(CLK_out));
  Register A (.D(out_7), .CLK(CLK_out), .RI(rom_1_data[15]), .RO(rom_1_data[14]), .Q(out_7), .V(out_2));
  Register B (.D(out_7), .CLK(CLK_out), .RI(rom_1_data[13]), .RO(rom_1_data[12]), .Q(out_7), .V(out_6));
  assign out_7 = rom_1_data[11] ? E__ALU : 8'bz;  // Controlled_Buffer controlled_buffer_1
  Adder adder_1 (.a(out_2), .b(out_6), .out(E__ALU));  // open: cin, cout
  assign out_7 = rom_1_data[10] ? I__Input : 8'bz;  // Controlled_Buffer controlled_buffer_2
  Register register_1 (.D(out_7), .CLK(CLK_out), .RI(rom_1_data[9]), .V(O__Output));  // open: RO, Q
  Register M_AR (.D(out_7), .CLK(CLK_out), .RI(rom_1_data[8]), .V(MAR));  // open: RO, Q
  assign out_7 = rom_1_data[7] ? ram_1_data : 8'bz;  // Controlled_Buffer controlled_buffer_3
  RAM ram_1 (.addr(MAR), .data(ram_1_data), .clk(CLK_out));  // open: sel, ld, clr
  ROM #(.addrWidth(16), .dataWidth(16)) rom_1 (.data(rom_1_data));  // open: addr, sel

  // Notes on the sheet:
  //   SAP-1 inspireret 8 bit computer - version 3
  //   Michell Cronberg
  //   AI
  //   AO
  //   BI
  //   IO
  //   BO
  //   EO
  //   8 bit databus
  //   MI
  //   OI
  //   RO
  //   PE
  //   (R)AM
endmodule

module Register (
  input  RO,
  input  [7:0] D,
  input  CLK,
  input  RI,
  output [7:0] Q,
  output [7:0] V
);

  wire [7:0] controlled_buffer_1_out;

  assign controlled_buffer_1_out = RI ? D : 8'bz;  // Controlled_Buffer controlled_buffer_1
  Register_part register_1 (.D(controlled_buffer_1_out), .en(1'b1), .Q(V), .clk(CLK), .clr(1'b0));
  assign Q = RO ? V : 8'bz;  // Controlled_Buffer controlled_buffer_2
endmodule

module ProgramCounter (
  input  S,
  input  [7:0] A,
  input  Count,
  input  Reset,
  output [7:0] Q
);

  wire not_1_out;

  not not_1 (not_1_out, S);
  Counter counter_1 (.load(S), .D(A), .count(not_1_out), .Q(Q), .clk(Count), .clr(Reset));  // open: carry
endmodule
